// Logisim project Simple CPU.circ as structural Verilog: 12 circuits, main circuit 1 Bit ALU
// ALU 0
module _1_Bit_ALU (
  input  Operand_B,
  input  Operand_A,
  input  [2:0] Operation,
  input  Carry_In,
  input  Binvert,
  output Result0,
  output Carry0
);

  wire adder_1_out, and_1_out, multiplexer_1_out, not_1_out, or_1_out, xnor_1_out, xor_1_out;

  not not_1 (not_1_out, Operand_B);
  Multiplexer multiplexer_1 (.in0(Operand_B), .in1(not_1_out), .out(multiplexer_1_out), .sel(Binvert));  // open: en
  and and_1 (and_1_out, Operand_A, multiplexer_1_out);
  or or_1 (or_1_out, Operand_A, multiplexer_1_out);
  ExactlyOne xor_1 (.out(xor_1_out), .in0(Operand_A), .in1(Operand_A), .in2(Operand_B));
  xnor xnor_1 (xnor_1_out, Operand_A, Operand_B);
  Adder #(.width(1)) adder_1 (.a(Operand_A), .b(Operand_B), .out(adder_1_out), .cin(Carry_In), .cout(Carry0));
  Multiplexer #(.select(3)) multiplexer_2 (
    .in2(and_1_out), .in3(or_1_out), .in4(xor_1_out), .in5(xnor_1_out), .in6(adder_1_out), .out(Result0),
    .sel(Operation));  // open: in0, in1, in7, en
endmodule

module _16_bit_ALU (
  input  Carry_In,
  input  [15:0] Operand_A,
  input  [15:0] Operand_B,
  input  [2:0] Operation,
  input  Binvert,
  output zero,
  output [15:0] result,
  output Carry15,
  output Overflow
);

  wire n1_bit_alu_1_carry0, n1_bit_alu_2_carry0, n1_bit_alu_3_carry0, n1_bit_alu_4_carry0,
       n1_bit_alu_5_carry0, n1_bit_alu_6_carry0, n1_bit_alu_7_carry0, n1_bit_alu_8_carry0,
       n1_bit_alu_9_carry0, n1_bit_alu_10_carry0, n1_bit_alu_11_carry0, n1_bit_alu_12_carry0,
       n1_bit_alu_13_carry0, n1_bit_alu_14_carry0, n1_bit_alu_15_carry0;

  _1_Bit_ALU u_1_bit_alu_1 (
    .Result0(result[0]), .Carry0(n1_bit_alu_1_carry0), .Operand_B(Operand_B[0]), .Operand_A(Operand_A[0]),
    .Binvert(Binvert), .Operation(Operation));  // open: Carry_In
  _1_Bit_ALU u_1_bit_alu_2 (
    .Result0(result[1]), .Carry0(n1_bit_alu_2_carry0), .Operand_B(Operand_B[1]), .Operand_A(Operand_A[1]),
    .Binvert(Binvert), .Operation(Operation));  // open: Carry_In
  _1_Bit_ALU u_1_bit_alu_3 (
    .Result0(result[2]), .Carry0(n1_bit_alu_3_carry0), .Operand_B(Operand_B[2]), .Operand_A(Operand_A[2]),
    .Binvert(Binvert), .Operation(Operation));  // open: Carry_In
  _1_Bit_ALU u_1_bit_alu_4 (
    .Result0(result[3]), .Carry0(n1_bit_alu_4_carry0), .Operand_B(Operand_B[3]), .Operand_A(Operand_A[3]),
    .Binvert(Binvert), .Operation(Operation));  // open: Carry_In
  _1_Bit_ALU u_1_bit_alu_5 (
    .Result0(result[4]), .Carry0(n1_bit_alu_5_carry0), .Operand_B(Operand_B[4]), .Operand_A(Operand_A[4]),
    .Binvert(Binvert), .Operation(Operation));  // open: Carry_In
  _1_Bit_ALU u_1_bit_alu_6 (
    .Result0(result[5]), .Carry0(n1_bit_alu_6_carry0), .Operand_B(Operand_B[5]), .Operand_A(Operand_A[5]),
    .Binvert(Binvert), .Operation(Operation));  // open: Carry_In
  _1_Bit_ALU u_1_bit_alu_7 (
    .Result0(result[6]), .Carry0(n1_bit_alu_7_carry0), .Operand_B(Operand_B[6]), .Operand_A(Operand_A[6]),
    .Binvert(Binvert), .Operation(Operation));  // open: Carry_In
  _1_Bit_ALU u_1_bit_alu_8 (
    .Result0(result[7]), .Carry0(n1_bit_alu_8_carry0), .Operand_B(Operand_B[7]), .Operand_A(Operand_A[7]),
    .Binvert(Binvert), .Operation(Operation));  // open: Carry_In
  _1_Bit_ALU u_1_bit_alu_9 (
    .Result0(result[8]), .Carry0(n1_bit_alu_9_carry0), .Operand_B(Operand_B[8]), .Operand_A(Operand_A[8]),
    .Binvert(Binvert), .Operation(Operation));  // open: Carry_In
  _1_Bit_ALU u_1_bit_alu_10 (
    .Result0(result[9]), .Carry0(n1_bit_alu_10_carry0), .Operand_B(Operand_B[9]), .Operand_A(Operand_A[9]),
    .Binvert(Binvert), .Operation(Operation));  // open: Carry_In
  _1_Bit_ALU u_1_bit_alu_11 (
    .Result0(result[10]), .Carry0(n1_bit_alu_11_carry0), .Operand_B(Operand_B[10]),
    .Operand_A(Operand_A[10]), .Binvert(Binvert), .Operation(Operation));  // open: Carry_In
  _1_Bit_ALU u_1_bit_alu_12 (
    .Result0(result[11]), .Carry0(n1_bit_alu_12_carry0), .Operand_B(Operand_B[11]),
    .Operand_A(Operand_A[11]), .Binvert(Binvert), .Operation(Operation));  // open: Carry_In
  _1_Bit_ALU u_1_bit_alu_13 (
    .Result0(result[12]), .Carry0(n1_bit_alu_13_carry0), .Operand_B(Operand_B[12]),
    .Operand_A(Operand_A[12]), .Binvert(Binvert), .Operation(Operation));  // open: Carry_In
  _1_Bit_ALU u_1_bit_alu_14 (
    .Result0(result[13]), .Carry0(n1_bit_alu_14_carry0), .Operand_B(Operand_B[13]),
    .Operand_A(Operand_A[13]), .Binvert(Binvert), .Operation(Operation));  // open: Carry_In
  _1_Bit_ALU u_1_bit_alu_15 (
    .Result0(result[14]), .Carry0(n1_bit_alu_15_carry0), .Operand_B(Operand_B[14]),
    .Operand_A(Operand_A[14]), .Binvert(Binvert), .Operation(Operation));  // open: Carry_In
  _1_Bit_ALU u_1_bit_alu_16 (
    .Result0(result[15]), .Carry0(Carry15), .Operand_B(Operand_B[15]), .Operand_A(Operand_A[15]),
    .Binvert(Binvert), .Operation(Operation));  // open: Carry_In
  xor xor_1 (Overflow, n1_bit_alu_15_carry0, Carry15);
  nor nor_1 (zero, result[0], result[1], result[2], result[3], result[4], result[5], result[6], result[7], result[8], result[9], result[10], result[11], result[12], result[13], result[14], result[15]);

  // Other names for the same wires on the sheet: A0 = Operand_A[0]; A1 = Operand_A[1]; A2 = Operand_A[2];
  //   A3 = Operand_A[3]; A4 = Operand_A[4]; A5 = Operand_A[5]; A6 = Operand_A[6]; A7 = Operand_A[7];
  //   A8 = Operand_A[8]; A9 = Operand_A[9]; A10 = Operand_A[10]; A11 = Operand_A[11]; A12 = Operand_A[12];
  //   A13 = Operand_A[13]; A14 = Operand_A[14]; A15 = Operand_A[15]; B0 = Operand_B[0]; B1 = Operand_B[1];
  //   B2 = Operand_B[2]; B3 = Operand_B[3]; B4 = Operand_B[4]; B5 = Operand_B[5]; B6 = Operand_B[6];
  //   B7 = Operand_B[7]; B8 = Operand_B[8]; B9 = Operand_B[9]; B10 = Operand_B[10]; B11 = Operand_B[11];
  //   B12 = Operand_B[12]; B13 = Operand_B[13]; B14 = Operand_B[14]; B15 = Operand_B[15]
endmodule

// PC
module Program_Counter (
  input  in_1,
  input  [11:0] in_2,
  input  in_3,
  input  in_4,
  input  in_5,
  output [11:0] out_6,
  output out_7
);

  Counter #(.width(12), .max('hfff)) counter_1 (
    .load(in_1), .D(in_2), .count(in_3), .Q(out_6), .carry(out_7), .clk(in_4), .clr(in_5));
endmodule

// MAR
module _12_bit_MAR (
  input  [11:0] in_1,
  input  in_2,
  input  in_3,
  input  in_4,
  output [11:0] out_5
);

  Register #(.width(12)) register_1 (.D(in_1), .en(in_2), .Q(out_5), .clk(in_3), .clr(in_4));
endmodule

// AC
module _16_bit_AC (
  input  [15:0] in_1,
  input  in_2,
  input  in_3,
  input  in_4,
  output [15:0] out_5
);

  Register #(.width(16)) register_1 (.D(in_1), .en(in_2), .Q(out_5), .clk(in_3), .clr(in_4));
endmodule

// MBR
module _16_bit_MBR (
  input  [15:0] in_1,
  input  in_2,
  input  in_3,
  input  in_4,
  output [15:0] out_5
);

  Register #(.width(16)) register_1 (.D(in_1), .en(in_2), .Q(out_5), .clk(in_3), .clr(in_4));
endmodule

// OUTreg
module _8_bit_input_register (
  input  [7:0] in_1,
  input  in_2,
  input  in_3,
  input  in_4,
  output [7:0] out_5
);

  Register register_1 (.D(in_1), .en(in_2), .Q(out_5), .clk(in_3), .clr(in_4));
endmodule

// InReg
module _8_bit_Output_register (
  input  [7:0] in_1,
  input  in_2,
  input  in_3,
  input  in_4,
  output [7:0] out_5
);

  Register register_1 (.D(in_1), .en(in_2), .Q(out_5), .clk(in_3), .clr(in_4));
endmodule

// Main Memory
module Memory_RAM (
  input  in_1,
  input  in_2
);

  wire clock_1_out, controlled_buffer_1_out;
  wire [6:0] ram_1_data, random_1_out;
  wire [7:0] counter_1_q;

  assign controlled_buffer_1_out = in_1 ? clock_1_out : 1'bz;  // Controlled_Buffer controlled_buffer_1
  Clock #(.highDuration(100), .lowDuration(100)) clock_1 (.out(clock_1_out));
  Counter #(.ongoal("stay")) counter_1 (
    .Q(counter_1_q), .clk(controlled_buffer_1_out));  // open: load, D, count, carry, clr
  Random #(.width(7)) random_1 (.clk(clock_1_out), .out(random_1_out));  // open: next, clr
  assign controlled_buffer_1_out = in_2 ? clock_1_out : 1'bz;  // Controlled_Buffer controlled_buffer_2
  RAM #(.dataWidth(7), .bus("separate")) ram_1 (
    .addr(counter_1_q), .din(random_1_out), .data(ram_1_data), .clk(controlled_buffer_1_out));  // open: str, sel, ld, clr
  TTY #(.rows(32)) tty_1 (.data(ram_1_data), .clk(controlled_buffer_1_out));  // open: we, clr
endmodule

module Sequence_detector (
  input  X,
  output OutPut
);

  wire and_1_out, and_2_out, and_3_out, and_4_out, clock_1_out, d_ff_1_q, d_ff_1_qn, d_ff_2_q, d_ff_2_qn,
       or_1_out, or_2_out;

  and and_1 (and_1_out, X, d_ff_1_q);
  and and_2 (and_2_out, X, d_ff_1_q, d_ff_2_q);
  and and_3 (and_3_out, X, d_ff_1_qn);
  and and_4 (and_4_out, X, d_ff_2_qn);
  Clock clock_1 (.out(clock_1_out));
  or or_1 (or_1_out, and_1_out, d_ff_2_q);
  or or_2 (or_2_out, and_2_out, and_3_out, and_4_out);
  D_Flip_Flop d_ff_1 (.clk(clock_1_out), .D(or_1_out), .Q(d_ff_1_q), .Qn(d_ff_1_qn));  // open: preset, en, reset
  D_Flip_Flop d_ff_2 (.clk(clock_1_out), .D(or_2_out), .Q(d_ff_2_q), .Qn(d_ff_2_qn));  // open: preset, en, reset
  and and_5 (OutPut, ~X, d_ff_1_q, d_ff_2_q);  // AND_Gate

  // Notes on the sheet:
  //   A
  //   B
endmodule

module Control_Unit (
);

  wire n16_bit_mbr_1_p1, n16_bit_mbr_1_p2, program_counter_1_out_7, undriven, undriven_2, undriven_3;
  wire [11:0] n12_bit_mar_1_out_5;

  _16_bit_ALU u_16_bit_alu_1 (
    .Binvert(undriven), .Carry_In(undriven_2));  // open: Operand_A, Operand_B, Operation, result, Carry15, Overflow, zero
  // _16_bit_MBR 16_bit_mbr_1: pin names not known; wires that end beside it: n16_bit_mbr_1_p1, n16_bit_mbr_1_p2
  Program_Counter program_counter_1 (.out_7(program_counter_1_out_7));  // open: in_1, in_2, in_3, in_4, in_5, out_6
  // _16_bit_AC 16_bit_ac_1: pin names not known; wires that end beside it: n16_bit_mbr_1_p2, n16_bit_mbr_1_p1
  _12_bit_MAR u_12_bit_mar_1 (.in_3(undriven_3), .out_5(n12_bit_mar_1_out_5));  // open: in_1, in_2, in_4
  _16_bit_IR u_16_bit_ir_1 (.in_2(program_counter_1_out_7));  // open: in_1, in_3, in_4, out_5
  _8_bit_input_register u_8_bit_input_register_1 (.in_2(undriven_2));  // open: in_1, in_3, in_4, out_5
  _8_bit_Output_register u_8_bit_output_register_1 (.in_3(undriven));  // open: in_1, in_2, in_4, out_5
  Memory_RAM memory_ram_1 (.in_2(undriven_3));  // open: in_1
endmodule

// IR
module _16_bit_IR (
  input  [15:0] in_1,
  input  in_2,
  input  in_3,
  input  in_4,
  output [15:0] out_5
);

  Register #(.width(16)) register_1 (.D(in_1), .en(in_2), .Q(out_5), .clk(in_3), .clr(in_4));
endmodule
